# Fritzing sketch scope_v2 (saved by Fritzing 0.9.3b)
circuit board: 8.46667cm x 5.64444cm

parts:
  RFID1 = ArduCam
  Part1 = Arduino Uno (Rev3)
  Zeiss_trigger_OUT = Power plug
  C1_100uF1 = Electrolytic Capacitor [capacitance=1µF package="100 mil [THT, electrolytic]"]
  M2 = Stepper Motor - Unipolar
  M3 = xy-mos d4184 [package=THT]
  MD09B1 = Pololu A4988 [package=SO16]
  LED1 = LEDs [package=led10mm]
  M4 = xy-mos d4184 [package=THT]
  Main_Power_12V = Power plug
  S1 = SWITCH-SPST-2 [package=switch-spst-vertical]
  Pololu_A1 = Pololu A4988 [package=SO16]
  4_7kΩ = Resistor [tolerance=±5% resistance=4.7k package="0402 [SMD]"]
  Peltiere = Peltier Element
  J2 = Power Jack [package=power_jack_slot]
  J3 = Power Plug
  M5 = Stepper Motor - Unipolar
  10k_NTC = Temperature Sensor (Thermistor) [thermistor_type=NTC package=THT]  # not connected
  Part2 = Arduino Uno (Rev3)  # not connected
  DRV_1 = Pololu DRV 8825 Stepper Motor Carrier, High Current [package=SO16]  # not connected
  Main_Power_12V_2 = Power plug
  J4 = Power Jack [package=power_jack_slot]
  J5 = Power Plug
  Peltiere_2 = Peltier Element
  Part4 = ws2812b [package="smd 2812b"]
  4_7_kΩ = Resistor [tolerance=±5% resistance=4.7k package="0402 [SMD]"]
  Camera_motor = Stepper Motor - Unipolar
  Axial_motor = Stepper Motor - Unipolar
  DRV_2 = Pololu DRV 8825 Stepper Motor Carrier, High Current [package=SO16]
  Arduino_CNC_Shield_V3_00_2 = Arduino_CNC_V3.00
  10kΩ = Resistor [tolerance=±5% resistance=10k package="0402 [SMD]"]
  10k_NTC_2 = Temperature Sensor (Thermistor) [thermistor_type=NTC package=THT]
  Zeiss_trigger_IN = Power plug
  Part5 = IFR520 MOS module [package=THT]

nets (from the breadboard view):
  N1: RFID1.CS, Arduino_CNC_Shield_V3_00_2.End_Stops_Y+_(and_Y-)
  N2: RFID1.MOSI, Arduino_CNC_Shield_V3_00_2.End_Stops_Z+_(and_Z-)_/_SpnEn
  N3: RFID1.MISO, Arduino_CNC_Shield_V3_00_2.SpnEn_/_Z_Limit
  N4: RFID1.SCK, Arduino_CNC_Shield_V3_00_2.SpnDir
  N5: RFID1.VCC, Arduino_CNC_Shield_V3_00_2.5V#75, 10kΩ.Pin_0, Part5.pin2
  N6: RFID1.GND, Arduino_CNC_Shield_V3_00_2.CoolEn_(Gnd)
  N7: RFID1.SDA, Arduino_CNC_Shield_V3_00_2.SDA
  N8: RFID1.SCL, Arduino_CNC_Shield_V3_00_2.SCL_/_Probe
  N9: Part1.A1, Zeiss_trigger_OUT.VCC, 4_7kΩ.Pin_0
  N10: Part1.D8, Pololu_A1.DIR
  GND: Part1.D9_PWM, Part1.D6_PWM, C1_100uF1.-, C1_100uF1.+, M3.PWM, M3.GND#2, M3.+, MD09B1.GND#14, MD09B1.VMOT, LED1.A, M4.PWM, M4.GND#2, M4.+, Main_Power_12V.GND, S1.P, Pololu_A1.GND#14, Pololu_A1.VMOT, Peltiere.pin1, J2.GND, J2.tip_GND, J3.GND, J3.tip_GND
  GND_2: Part1.GND, Zeiss_trigger_OUT.GND, M3.GND#1, M3.LOAD, MD09B1.GND#8, LED1.C, M4.GND#1, M4.LOAD, Pololu_A1.GND#8, 4_7kΩ.Pin_1, J2.GNDBREAK
  N11: Part1.D3_PWM, Pololu_A1.STEP
  N12: Part1.D4, MD09B1.DIR
  N13: Part1.D5_PWM, MD09B1.STEP
  N14: Part1.D7, MD09B1.ENABLE, Pololu_A1.ENABLE
  VDD: Part1.5V, MD09B1.MS1, MD09B1.MS2, MD09B1.MS3, MD09B1.VDD, Pololu_A1.MS1, Pololu_A1.MS2, Pololu_A1.MS3, Pololu_A1.VDD
  N15: M2.A, MD09B1.2B
  N16: M2.C, MD09B1.2A
  N17: M2.B, MD09B1.1A
  N18: M2.D, MD09B1.1B
  N19: MD09B1.RESET, MD09B1.SLEEP
  N20: Main_Power_12V.VCC, S1.O
  N21: Pololu_A1.RESET, Pololu_A1.SLEEP
  N22: Pololu_A1.1B, M5.D
  N23: Pololu_A1.1A, M5.B
  N24: Pololu_A1.2A, M5.C
  N25: Pololu_A1.2B, M5.A
  N26: Peltiere.pin2, J2.PWR, J2.tip_PWR, J3.PWR, J3.tip_PWR
  N27: Main_Power_12V_2.GND, Arduino_CNC_Shield_V3_00_2.POWER_-, Part5.pin5
  N28: Main_Power_12V_2.VCC, Arduino_CNC_Shield_V3_00_2.POWER_+, Arduino_CNC_Shield_V3_00_2.Hold_(Gnd), Part5.pin4
  GND_3: J4.GND, J4.tip_GND, J5.GND, J5.tip_GND, Peltiere_2.pin1, Part5.pin7
  N29: J4.PWR, J4.tip_PWR, J5.PWR, J5.tip_PWR, Peltiere_2.pin2
  N30: J4.GNDBREAK, Part5.pin6
  N31: Part4.VDD, Arduino_CNC_Shield_V3_00_2.5V#11
  VSS: Part4.VSS, Arduino_CNC_Shield_V3_00_2.GND
  N32: Part4.DIN, DRV_2.MS2, Arduino_CNC_Shield_V3_00_2.Y.DIR
  N33: 4_7_kΩ.Pin_0, Arduino_CNC_Shield_V3_00_2.Hold, Zeiss_trigger_IN.VCC
  N34: 4_7_kΩ.Pin_1, Arduino_CNC_Shield_V3_00_2.End_Stops_X-_(Gnd), Zeiss_trigger_IN.GND
  N35: Camera_motor.A, Arduino_CNC_Shield_V3_00_2.Z-MTR_'1'
  N36: Camera_motor.C, Arduino_CNC_Shield_V3_00_2.Z-MTR_'2'
  N37: Camera_motor.B, Arduino_CNC_Shield_V3_00_2.Z-MTR_'3'
  N38: Camera_motor.D, Arduino_CNC_Shield_V3_00_2.Z-MTR_'4'
  N39: Axial_motor.A, Arduino_CNC_Shield_V3_00_2.X-MTR_'1'
  N40: Axial_motor.C, Arduino_CNC_Shield_V3_00_2.X-MTR_'2'
  N41: Axial_motor.B, Arduino_CNC_Shield_V3_00_2.X-MTR_'3'
  N42: Axial_motor.D, Arduino_CNC_Shield_V3_00_2.X-MTR_'4'
  N43: Arduino_CNC_Shield_V3_00_2.Y.STEP, Part5.pin1
  N44: Arduino_CNC_Shield_V3_00_2.X_-_M2, Arduino_CNC_Shield_V3_00_2.X_-_M2_(5V)
  N45: Arduino_CNC_Shield_V3_00_2.Z_-_M2, Arduino_CNC_Shield_V3_00_2.Z_-_M2_(5V)
  N46: Arduino_CNC_Shield_V3_00_2.Abort, 10kΩ.Pin_1, 10k_NTC_2.pin_1
  N47: Arduino_CNC_Shield_V3_00_2.Resume_(Gnd), 10k_NTC_2.pin_0
  N48: Arduino_CNC_Shield_V3_00_2.E-STOP_(Gnd), Part5.pin3

custom parts:
  ArduCam: 5 MINI plus
  xy-mos d4184: xy-mos d4184 Two parallel N-Channel logic compatible MOSFETS with low Rds(on) for high current low-side switching applications.
  Power Jack: Power Jack This is the standard 5.5mm barrel jack for power. Ths one is modified to mate with the barrel plug part and allow the two to "connect" so batteries and wall warts can be "connected" in breadboard and will go through to schematic.
  Power Plug: Power Jack This is the standard 5.5mm barrel plug for power. This part has bendable leads (i.e. wires in the real world) to connect to wall warts or the breadboard in the standard wire end, and hidden connectors on the tip end that will connect when "plugged in" (overlapped with the jack so it appears "plugged in" in breadboard) to the modified coax jack part. Internal busses connect the two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
  Pololu DRV 8825 Stepper Motor Carrier, High Current: DRV 8825 This is a Stepper Motor Controller for integrated circuits. This breakout board for TI’s DRV8825 microstepping bipolar stepper motor driver features adjustable current limiting, over-current and over-temperature protection, and six microstep resolutions (down to 1/32-step). It operates from 8.2 V to 45 V and can deliver up to approximately 1.5 A per phase without a heat sink or forced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
  Arduino_CNC_V3.00: Protoneer Arduino CNC Shield V3.00 If using Grbl V0.9: The “A” axis can not be used (yet). The “SCL” (Arduino A5) pin is now used for 'Probing' input. The “End Stops Z+ & Z-” (Arduino D11) and “SpnEn” (Arduino D12) have been switched!
